# Fritzing sketch GreenhouseController (saved by Fritzing 0.9.9b)
breadboards: 1

parts:
  Part1 = Arduino Mega 2560 (Rev3)
  Part2 = Adafruit BME280
  Part3 = Adafruit TSL2561 [part_number="Adafruit #439"]
  DHT1 = DHT22 Humidity and Temperature Sensor
  DHT2 = DHT22 Humidity and Temperature Sensor
  Misting_Motor = LED - 5mm [color="Red (633nm)" current=0.030 package="5 mm [THT]"]
  R2 = Resistor [tolerance=±5% resistance=220 package="2010 [SMD]"]
  R3 = Resistor [tolerance=±5% resistance=220 package="2010 [SMD]"]
  R4 = Resistor [tolerance=±5% resistance=220 package="2010 [SMD]"]
  R5 = Resistor [tolerance=±5% resistance=220 package="2010 [SMD]"]
  Light = LED - 5mm [color="Red (633nm)" current=0.030 package="5 mm [THT]"]
  Ventilation_Fan = LED - 5mm [color="Red (633nm)" current=0.030 package="5 mm [THT]"]
  Circulating_Fan = LED - 5mm [color="Red (633nm)" current=0.030 package="5 mm [THT]"]
  Heater = LED - 5mm [color="Red (633nm)" current=0.030 package="5 mm [THT]"]
  R1 = Resistor [tolerance=±5% resistance=220 package="2010 [SMD]"]

nets:
  N1: Part1.D21/SCL, Part2.SCK/SCL, Part3.SCL
  N2: Part1.D20/SDA, Part1.SDA, Part2.SDI/SDA, Part3.SDA
  GND: Part1.GND, Part2.GND, Part3.GND, R2.Pin_0, R3.Pin_0, R4.Pin_0, R5.Pin_0, R1.Pin_0
  N3: Part1.D13_PWM, DHT1.DATA
  N4: Part1.D12_PWM, DHT2.DATA
  5V: Part1.5V, Part3.VIN, DHT1.VDD
  N5: Part1.D3_PWM, Heater.cathode
  N6: Part1.D4_PWM, Circulating_Fan.cathode
  N7: Part1.D5_PWM, Ventilation_Fan.cathode
  N8: Part1.D6_PWM, Light.cathode
  N9: Part1.D7_PWM, Misting_Motor.cathode
  VIN: Part2.VIN, DHT2.VDD
  GND_2: DHT1.GND, DHT2.GND
  N10: Misting_Motor.anode, R1.Pin_1
  N11: R2.Pin_1, Light.anode
  N12: R3.Pin_1, Ventilation_Fan.anode
  N13: R4.Pin_1, Circulating_Fan.anode
  N14: R5.Pin_1, Heater.anode

custom parts:
  Adafruit BME280: Bosch has stepped up their game with their new BME280 sensor, an environmental sensor with temperature, barometric pressure and humidity! This sensor is great for all sorts of weather/environmental sensing and can even be used in both I2C and SPI! This precision sensor from Bosch is the best low-cost sensing solution for measuring humidity with ±3% accuracy, barometric pressure with ±1 hPa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
  Adafruit TSL2561: The TSL2561 luminosity sensor is an advanced digital light sensor, ideal for use in a wide range of light situations. Compared to low cost CdS cells, this sensor is more precise, allowing for exact lux calculations and can be configured for different gain/timing ranges to detect light ranges from up to 0.1 - 40,000+ Lux on the fly. The best part of this sensor is that it contains both infrared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
